# Fritzing sketch CircuitDiagram (saved by Fritzing 0.9.6b)
breadboards: 2

parts:
  Raspberry_Pi_1 = Raspberry Pi 3 [part_number=RPI-3-V1.2]

nets:
  N1: Raspberry_Pi_1.GPIO3, Raspberry_Pi_1.GPIO22, Raspberry_Pi_1.GPIO23
  N2: Raspberry_Pi_1.GND, Raspberry_Pi_1.GPIO13, Raspberry_Pi_1.GPIO15
